# Fritzing sketch schematic (saved by Fritzing 0.9.5d)
breadboards: 1

parts:
  Part1 = Arduino Mega 2560 (Rev3)
  DHT11_1 = DHT11 module
  Part2 = RFID-RC522-v2
  YwRobot_Power_Supply1 = YwRobot Breadboard Power Supply [part_number=545043]
  U2 = LCD-16X2 [package=lcd-16x2_noholes]
  IR1 = TSOP312.., 314.. [package=THT]
  LED1 = smd LED [color="Red (633nm)" package="1206 [SMD]"]
  LED2 = smd LED [color="Red (633nm)" package="1206 [SMD]"]
  R1 = Resistor [tolerance=±5% resistance=1k package=THT]
  R2 = Resistor [tolerance=±5% resistance=1k package=THT]
  M1 = DC Motor
  IC1 = L293D [package=THT]
  J1 = Piezo Speaker
  Water_Level_Sensor1 = Water Level Sensor
  R3 = Trimmer Potentiometer [maximum_resistance=10kΩ package=THT]
  HC-SR04_Sensor_1 = HC-SR04 Ultrasonic Distance Sensor

nets:
  N1: Part1.A0, DHT11_1.DATA
  N2: Part1.A1, Water_Level_Sensor1.SIG
  GND: Part1.GND, DHT11_1.GND, Part2.GND, YwRobot_Power_Supply1.GND#13, YwRobot_Power_Supply1.GND#14, U2.VSS, U2.R_W, U2.A, U2.K, IR1.GND, R1.Pin_0, R2.Pin_0, IC1.0V, J1.pin1, Water_Level_Sensor1.GND, R3.leg2, HC-SR04_Sensor_1.GND
  N3: Part1.D13_PWM, J1.pin2
  N4: Part1.D12_PWM, HC-SR04_Sensor_1.ECHO
  N5: Part1.D11_PWM, U2.DB7
  N6: Part1.D10_PWM, U2.DB6
  N7: Part1.D9_PWM, U2.DB5
  N8: Part1.D8_PWM, U2.DB4
  3V3: Part1.3V3, Part2.3.3V, IR1.Vs
  VCC: Part1.5V, DHT11_1.VCC, U2.VDD, IC1.Enable_1, IC1.+V, HC-SR04_Sensor_1.VCC
  N9: Part1.D2_PWM, U2.RS
  N10: Part1.D3_PWM, U2.E
  N11: Part1.D4_PWM, Part2.RST
  N12: Part1.D5_PWM, IC1.In_2
  N13: Part1.D6_PWM, IC1.In_1
  N14: Part1.D7_PWM, LED1.cathode, LED2.anode
  N15: Part1.D22, IR1.Data
  N16: Part1.D31, HC-SR04_Sensor_1.TRIG
  N17: Part1.D49, Water_Level_Sensor1.VCC
  N18: Part1.D50, Part2.MISO
  N19: Part1.D51, Part2.MOSI
  N20: Part1.D52, Part2.SCK
  N21: Part1.D53, Part2.SDA
  N22: YwRobot_Power_Supply1.VCC#5, YwRobot_Power_Supply1.VCC#6
  N23: YwRobot_Power_Supply1.VCC#9, YwRobot_Power_Supply1.VCC#10, IC1.+Vmotor
  N24: YwRobot_Power_Supply1.GND#11, YwRobot_Power_Supply1.GND#12
  N25: U2.VO, R3.wiper
  N26: LED1.anode, R2.Pin_1
  N27: LED2.cathode, R1.Pin_1
  N28: M1.pin_1, IC1.Out_1_(_Controlled_by_Enable_1_)
  N29: M1.pin_2, IC1.Out_2_(_Controlled_by_Enable_1_)

custom parts:
  DHT11 module: DHT11 black pcb module
  RFID-RC522-v2: A simple China made RFID-RC522 Reader; do check the pin labels, as this is a MFRC522 based clone.
  YwRobot Breadboard Power Supply: The YwRobot Breadboard Power Supply (MB-V2) has two power rails; they can be 5V or 3V3. Power to the module can be provided through the female USB socket or through the A10 (female) 2.1mm power jack.
  Water Level Sensor: A water level sensor. This sensor operates at 3V to 5V. The Sig (signal) pin outputs an analogue signal that is in proportion to the amount of water in contact with the sensor.
