# Fritzing sketch schematic (saved by Fritzing 0.9.5d)
breadboards: 1

parts:
  Part1 = Arduino Mega 2560 (Rev3)
  LED1 = LED - 5mm [color="Red (633nm)" package="5 mm [THT]"]
  R1 = Resistor [tolerance=±5% resistance=10k package=THT]
  R3 = Photocell (LDR) [package=THT]
  R4 = Resistor [tolerance=±5% resistance=1k package=THT]

nets:
  N1: Part1.A0, LED1.cathode, R4.Pin_1
  N2: Part1.A1, R1.Pin_0, R3.pin_1
  N3: Part1.GND, R1.Pin_1, R4.Pin_0
  N4: Part1.5V, R3.pin_0
  N5: Part1.D6_PWM, LED1.anode
